// Logisim project 2107018_project.circ as structural Verilog: 9 circuits, main circuit main
module main (
);

  wire full_clock_1_hl0, full_clock_1_hl01, full_clock_1_hl02, full_clock_1_hl03, full_clock_1_hr0,
       full_clock_1_hr01, full_clock_1_hr02, full_clock_1_hr03, full_clock_1_ml0, full_clock_1_ml01,
       full_clock_1_ml02, full_clock_1_ml03, full_clock_1_mr0, full_clock_1_mr01, full_clock_1_mr02,
       full_clock_1_mr03, full_clock_1_sl0, full_clock_1_sl01, full_clock_1_sl02, full_clock_1_sl03,
       full_clock_1_sr0, full_clock_1_sr01, full_clock_1_sr02, full_clock_1_sr03, n7seg_1_a_2, n7seg_1_b_2,
       n7seg_1_c_2, n7seg_1_d_2, n7seg_1_e, n7seg_1_f, n7seg_1_g, n7seg_2_a_2, n7seg_2_b_2, n7seg_2_c_2,
       n7seg_2_d_2, n7seg_2_e, n7seg_2_f, n7seg_2_g, n7seg_3_a_2, n7seg_3_b_2, n7seg_3_c_2, n7seg_3_d_2,
       n7seg_3_e, n7seg_3_f, n7seg_3_g, n7seg_4_a_2, n7seg_4_b_2, n7seg_4_c_2, n7seg_4_d_2, n7seg_4_e,
       n7seg_4_f, n7seg_4_g, n7seg_5_a_2, n7seg_5_b_2, n7seg_5_c_2, n7seg_5_d_2, n7seg_5_e, n7seg_5_f,
       n7seg_5_g, n7seg_6_a_2, n7seg_6_b_2, n7seg_6_c_2, n7seg_6_d_2, n7seg_6_e, n7seg_6_f, n7seg_6_g;

  _7SEG u_7seg_1 (
    .A(full_clock_1_hl03), .B(full_clock_1_hl02), .C(full_clock_1_hl01), .D(full_clock_1_hl0),
    .a_2(n7seg_1_a_2), .b_2(n7seg_1_b_2), .c_2(n7seg_1_c_2), .d_2(n7seg_1_d_2), .e(n7seg_1_e), .f(n7seg_1_f),
    .g(n7seg_1_g));
  _7_Segment_Display u_7_segment_display_1 (
    .g(n7seg_1_g), .f(n7seg_1_f), .a(n7seg_1_a_2), .b(n7seg_1_b_2), .e(n7seg_1_e), .d(n7seg_1_d_2),
    .c(n7seg_1_c_2));  // open: dp
  _7SEG u_7seg_2 (
    .A(full_clock_1_hr03), .B(full_clock_1_hr02), .C(full_clock_1_hr01), .D(full_clock_1_hr0),
    .a_2(n7seg_2_a_2), .b_2(n7seg_2_b_2), .c_2(n7seg_2_c_2), .d_2(n7seg_2_d_2), .e(n7seg_2_e), .f(n7seg_2_f),
    .g(n7seg_2_g));
  _7_Segment_Display u_7_segment_display_2 (
    .g(n7seg_2_g), .f(n7seg_2_f), .a(n7seg_2_a_2), .b(n7seg_2_b_2), .e(n7seg_2_e), .d(n7seg_2_d_2),
    .c(n7seg_2_c_2));  // open: dp
  FULL_clock full_clock_1 (
    .ML03(full_clock_1_ml03), .ML02(full_clock_1_ml02), .ML01(full_clock_1_ml01), .ML0(full_clock_1_ml0),
    .MR03(full_clock_1_mr03), .MR02(full_clock_1_mr02), .MR01(full_clock_1_mr01), .MR0(full_clock_1_mr0),
    .SL03(full_clock_1_sl03), .SL02(full_clock_1_sl02), .SL01(full_clock_1_sl01), .SL0(full_clock_1_sl0),
    .SR03(full_clock_1_sr03), .SR02(full_clock_1_sr02), .SR01(full_clock_1_sr01), .SR0(full_clock_1_sr0),
    .HL03(full_clock_1_hl03), .HL02(full_clock_1_hl02), .HL01(full_clock_1_hl01), .HL0(full_clock_1_hl0),
    .HR03(full_clock_1_hr03), .HR02(full_clock_1_hr02), .HR01(full_clock_1_hr01), .HR0(full_clock_1_hr0));
  _7SEG u_7seg_3 (
    .A(full_clock_1_ml03), .B(full_clock_1_ml02), .C(full_clock_1_ml01), .D(full_clock_1_ml0),
    .a_2(n7seg_3_a_2), .b_2(n7seg_3_b_2), .c_2(n7seg_3_c_2), .d_2(n7seg_3_d_2), .e(n7seg_3_e), .f(n7seg_3_f),
    .g(n7seg_3_g));
  _7_Segment_Display u_7_segment_display_3 (
    .g(n7seg_3_g), .f(n7seg_3_f), .a(n7seg_3_a_2), .b(n7seg_3_b_2), .e(n7seg_3_e), .d(n7seg_3_d_2),
    .c(n7seg_3_c_2));  // open: dp
  _7SEG u_7seg_4 (
    .A(full_clock_1_mr03), .B(full_clock_1_mr02), .C(full_clock_1_mr01), .D(full_clock_1_mr0),
    .a_2(n7seg_4_a_2), .b_2(n7seg_4_b_2), .c_2(n7seg_4_c_2), .d_2(n7seg_4_d_2), .e(n7seg_4_e), .f(n7seg_4_f),
    .g(n7seg_4_g));
  _7_Segment_Display u_7_segment_display_4 (
    .g(n7seg_4_g), .f(n7seg_4_f), .a(n7seg_4_a_2), .b(n7seg_4_b_2), .e(n7seg_4_e), .d(n7seg_4_d_2),
    .c(n7seg_4_c_2));  // open: dp
  _7SEG u_7seg_5 (
    .A(full_clock_1_sl03), .B(full_clock_1_sl02), .C(full_clock_1_sl01), .D(full_clock_1_sl0),
    .a_2(n7seg_5_a_2), .b_2(n7seg_5_b_2), .c_2(n7seg_5_c_2), .d_2(n7seg_5_d_2), .e(n7seg_5_e), .f(n7seg_5_f),
    .g(n7seg_5_g));
  _7_Segment_Display u_7_segment_display_5 (
    .g(n7seg_5_g), .f(n7seg_5_f), .a(n7seg_5_a_2), .b(n7seg_5_b_2), .e(n7seg_5_e), .d(n7seg_5_d_2),
    .c(n7seg_5_c_2));  // open: dp
  _7SEG u_7seg_6 (
    .A(full_clock_1_sr03), .B(full_clock_1_sr02), .C(full_clock_1_sr01), .D(full_clock_1_sr0),
    .a_2(n7seg_6_a_2), .b_2(n7seg_6_b_2), .c_2(n7seg_6_c_2), .d_2(n7seg_6_d_2), .e(n7seg_6_e), .f(n7seg_6_f),
    .g(n7seg_6_g));
  _7_Segment_Display u_7_segment_display_6 (
    .g(n7seg_6_g), .f(n7seg_6_f), .a(n7seg_6_a_2), .b(n7seg_6_b_2), .e(n7seg_6_e), .d(n7seg_6_d_2),
    .c(n7seg_6_c_2));  // open: dp

  // Notes on the sheet:
  //   2107018
endmodule

module SECOND_RIGHT (
  input  TT1,
  output Q3,
  output Q2,
  output Q1,
  output Q0,
  output CLOCKO,
  output SK01
);

  wire and_1_out, and_3_out, and_4_out, clock_1_out, not_1_out, Q1_qn, Q2_qn, Q3_qn;

  Clock clock_1 (.out(clock_1_out));
  and and_1 (and_1_out, Q3_qn, Q0);
  J_K_Flip_Flop u_Q3 (.J(and_3_out), .clk(clock_1_out), .K(Q0), .Q(Q3), .Qn(Q3_qn), .preset(TT1));  // open: en, reset
  and and_2 (SK01, not_1_out, Q2, Q1, Q0);
  and and_3 (and_3_out, Q0, Q1, Q2);
  nand nand_1 (CLOCKO, Q3, Q2_qn, Q1_qn, Q0);
  not not_1 (not_1_out, Q3);
  J_K_Flip_Flop u_Q2 (
    .J(and_4_out), .clk(clock_1_out), .K(and_4_out), .Q(Q2), .Qn(Q2_qn), .reset(TT1));  // open: preset, en
  and and_4 (and_4_out, Q1, Q0);
  J_K_Flip_Flop u_Q1 (.J(and_1_out), .clk(clock_1_out), .K(Q0), .Q(Q1), .Qn(Q1_qn), .reset(TT1));  // open: preset, en
  J_K_Flip_Flop u_Q0 (.J(1'b1), .clk(clock_1_out), .K(1'b1), .Q(Q0), .reset(TT1));  // open: Qn, preset, en

  // Notes on the sheet:
  //   2107018
endmodule

module SECOND_LEFT (
  input  TT2,
  input  CLOCK0I,
  output Q3,
  output Q2,
  output Q1,
  output Q0,
  output CLOCKO,
  output SK02
);

  wire and_2_out, and_3_out, Q1_qn, Q2_qn, Q3_qn;

  nand nand_1 (CLOCKO, Q3_qn, Q2, Q1_qn, Q0);
  and and_1 (SK02, Q3_qn, Q2_qn, Q1_qn, Q0);
  J_K_Flip_Flop u_Q3 (.J(1'b0), .clk(CLOCK0I), .K(1'b0), .Q(Q3), .Qn(Q3_qn), .reset(TT2));  // open: preset, en
  and and_2 (and_2_out, Q2_qn, Q0);
  J_K_Flip_Flop u_Q2 (.J(and_3_out), .clk(CLOCK0I), .K(Q0), .Q(Q2), .Qn(Q2_qn), .reset(TT2));  // open: preset, en
  and and_3 (and_3_out, Q0, Q1);
  J_K_Flip_Flop u_Q1 (
    .J(and_2_out), .clk(CLOCK0I), .K(and_2_out), .Q(Q1), .Qn(Q1_qn), .reset(TT2));  // open: preset, en
  J_K_Flip_Flop u_Q0 (.J(1'b1), .clk(CLOCK0I), .K(1'b1), .Q(Q0), .preset(TT2));  // open: Qn, en, reset
endmodule

module MINUTE_RIIGHT (
  input  clock0,
  input  TT1,
  output Q3,
  output Q2,
  output Q1,
  output Q0,
  output CLOCKO,
  output SK_7
);

  wire and_1_out, and_3_out, and_4_out, not_1_out, Q1_qn, Q2_qn, Q3_qn;

  and and_1 (and_1_out, Q0, Q1, Q2);
  J_K_Flip_Flop u_Q3 (.J(and_1_out), .clk(clock0), .K(Q0), .Q(Q3), .Qn(Q3_qn), .preset(TT1));  // open: en, reset
  and and_2 (SK_7, not_1_out, Q2, Q1, Q0);
  not not_1 (not_1_out, Q3);
  J_K_Flip_Flop u_Q2 (.J(and_3_out), .clk(clock0), .K(and_3_out), .Q(Q2), .Qn(Q2_qn), .reset(TT1));  // open: preset, en
  and and_3 (and_3_out, Q1, Q0);
  nand nand_1 (CLOCKO, Q3, Q2_qn, Q1_qn, Q0);
  and and_4 (and_4_out, Q3_qn, Q0);
  J_K_Flip_Flop u_Q1 (.J(and_4_out), .clk(clock0), .K(Q0), .Q(Q1), .Qn(Q1_qn), .reset(TT1));  // open: preset, en
  J_K_Flip_Flop u_Q0 (.J(1'b1), .clk(clock0), .K(1'b1), .Q(Q0), .reset(TT1));  // open: Qn, preset, en
endmodule

module MINUTE_LEFT (
  input  TT2,
  input  CLOCK0I,
  output Q3,
  output Q2,
  output Q1,
  output Q0,
  output CLOCKO,
  output SK02
);

  wire and_2_out, and_3_out, Q1_qn, Q2_qn, Q3_qn;

  nand nand_1 (CLOCKO, Q3_qn, Q2, Q1_qn, Q0);
  and and_1 (SK02, Q3_qn, Q2_qn, Q1_qn, Q0);
  J_K_Flip_Flop u_Q3 (.J(1'b0), .clk(CLOCK0I), .K(1'b0), .Q(Q3), .Qn(Q3_qn), .reset(TT2));  // open: preset, en
  and and_2 (and_2_out, Q2_qn, Q0);
  J_K_Flip_Flop u_Q2 (.J(and_3_out), .clk(CLOCK0I), .K(Q0), .Q(Q2), .Qn(Q2_qn), .reset(TT2));  // open: preset, en
  and and_3 (and_3_out, Q0, Q1);
  J_K_Flip_Flop u_Q1 (
    .J(and_2_out), .clk(CLOCK0I), .K(and_2_out), .Q(Q1), .Qn(Q1_qn), .reset(TT2));  // open: preset, en
  J_K_Flip_Flop u_Q0 (.J(1'b1), .clk(CLOCK0I), .K(1'b1), .Q(Q0), .preset(TT2));  // open: Qn, en, reset
endmodule

module hour_right (
  input  clk0,
  input  T5,
  output Q3,
  output Q2,
  output Q1,
  output Q0,
  output S5,
  output CLK0_2
);

  wire and_2_out, and_3_out, and_4_out, not_1_out, not_2_out, not_3_out, not_4_out, Q3_qn;

  and and_1 (S5, Q2, not_1_out, not_3_out, not_4_out);
  J_K_Flip_Flop u_Q0 (.J(1'b1), .clk(clk0), .K(1'b1), .Q(Q0), .reset(T5));  // open: Qn, preset, en
  not not_1 (not_1_out, Q3);
  J_K_Flip_Flop u_Q1 (.J(and_2_out), .clk(clk0), .K(Q0), .Q(Q1), .reset(T5));  // open: Qn, preset, en
  and and_2 (and_2_out, Q0, Q3_qn);
  not not_2 (not_2_out, Q2);
  and and_3 (and_3_out, Q1, Q0);
  not not_3 (not_3_out, Q1);
  not not_4 (not_4_out, Q0);
  J_K_Flip_Flop u_Q2 (.J(and_3_out), .clk(clk0), .K(and_3_out), .Q(Q2), .reset(T5));  // open: Qn, preset, en
  and and_4 (and_4_out, Q0, Q1, Q2);
  J_K_Flip_Flop u_Q3 (.J(and_4_out), .clk(clk0), .K(Q0), .Q(Q3), .Qn(Q3_qn), .reset(T5));  // open: preset, en
  nand nand_1 (CLK0_2, Q3, not_2_out, not_3_out, Q0);
endmodule

module hour_left (
  input  clk0,
  input  T6,
  output Q3,
  output Q2,
  output Q1,
  output Q0,
  output S6
);

  wire not_1_out, not_2_out, not_3_out, Q1_qn;

  J_K_Flip_Flop u_Q0 (.J(Q1_qn), .clk(clk0), .K(1'b1), .Q(Q0), .reset(T6));  // open: Qn, preset, en
  and and_1 (S6, not_3_out, not_2_out, Q1, not_1_out);
  J_K_Flip_Flop u_Q1 (.J(Q0), .clk(clk0), .K(1'b1), .Q(Q1), .Qn(Q1_qn), .reset(T6));  // open: preset, en
  J_K_Flip_Flop u_Q2 (.J(1'b0), .clk(clk0), .K(1'b0), .Q(Q2), .reset(T6));  // open: Qn, preset, en
  not not_1 (not_1_out, Q0);
  not not_2 (not_2_out, Q2);
  not not_3 (not_3_out, Q3);
  J_K_Flip_Flop u_Q3 (.J(1'b0), .clk(clk0), .K(1'b0), .Q(Q3), .reset(T6));  // open: Qn, preset, en
endmodule

module FULL_clock (
  output SL03,
  output SL02,
  output MR03,
  output SL01,
  output SL0,
  output SR02,
  output MR02,
  output SR03,
  output SR01,
  output SR0,
  output ML03,
  output ML02,
  output ML01,
  output ML0,
  output MR01,
  output MR0,
  output HR0,
  output HR01,
  output HR02,
  output HL0,
  output HR03,
  output HL01,
  output HL02,
  output HL03
);

  wire and_1_out, and_2_out, and_3_out, hour_left_1_s6, hour_right_1_clk0_2, hour_right_1_s5,
       minute_left_1_clocko, minute_left_1_sk02, minute_riight_1_clocko, minute_riight_1_sk_7,
       second_left_1_clocko, second_left_1_sk02, second_right_1_clocko, second_right_1_sk01;

  and and_1 (and_1_out, hour_left_1_s6, hour_right_1_s5);
  hour_left hour_left_1 (
    .clk0(hour_right_1_clk0_2), .T6(and_1_out), .S6(hour_left_1_s6), .Q3(HL03), .Q2(HL02), .Q1(HL01), .Q0(HL0));
  hour_right hour_right_1 (
    .clk0(minute_left_1_clocko), .T5(and_1_out), .S5(hour_right_1_s5), .CLK0_2(hour_right_1_clk0_2),
    .Q3(HR03), .Q2(HR02), .Q1(HR01), .Q0(HR0));
  MINUTE_LEFT minute_left_1 (
    .TT2(and_2_out), .CLOCK0I(minute_riight_1_clocko), .CLOCKO(minute_left_1_clocko),
    .SK02(minute_left_1_sk02), .Q3(ML03), .Q2(ML02), .Q1(ML01), .Q0(ML0));
  and and_2 (and_2_out, minute_left_1_sk02, minute_riight_1_sk_7);
  MINUTE_RIIGHT minute_riight_1 (
    .clock0(second_left_1_clocko), .TT1(and_2_out), .SK_7(minute_riight_1_sk_7), .Q3(MR03), .Q2(MR02),
    .Q1(MR01), .Q0(MR0), .CLOCKO(minute_riight_1_clocko));
  SECOND_LEFT second_left_1 (
    .TT2(and_3_out), .CLOCK0I(second_right_1_clocko), .CLOCKO(second_left_1_clocko),
    .SK02(second_left_1_sk02), .Q3(SL03), .Q2(SL02), .Q1(SL01), .Q0(SL0));
  and and_3 (and_3_out, second_left_1_sk02, second_right_1_sk01);
  SECOND_RIGHT second_right_1 (
    .TT1(and_3_out), .SK01(second_right_1_sk01), .Q3(SR03), .Q2(SR02), .Q1(SR01), .Q0(SR0),
    .CLOCKO(second_right_1_clocko));
endmodule

module _7SEG (
  input  A,
  input  B,
  input  C,
  input  D,
  output a_2,
  output b_2,
  output c_2,
  output d_2,
  output e,
  output f,
  output g
);

  wire and_1_out, and_2_out, and_3_out, and_4_out, and_5_out, and_6_out, and_7_out, and_8_out, and_9_out,
       not_1_out, not_2_out, not_3_out, xnor_1_out, xnor_2_out;

  not not_1 (not_1_out, B);
  not not_2 (not_2_out, C);
  not not_3 (not_3_out, D);
  xnor xnor_1 (xnor_1_out, B, D);
  xnor xnor_2 (xnor_2_out, C, D);
  and and_1 (and_1_out, not_1_out, not_3_out);
  and and_2 (and_2_out, not_3_out, C);
  and and_3 (and_3_out, not_1_out, C);
  and and_4 (and_4_out, C, not_3_out);
  and and_5 (and_5_out, not_1_out, not_3_out);
  and and_6 (and_6_out, B, not_2_out, D);
  and and_7 (and_7_out, not_2_out, not_3_out);
  and and_8 (and_8_out, B, not_2_out);
  and and_9 (and_9_out, B, not_3_out);
  or or_1 (a_2, xnor_1_out, A, C);
  or or_2 (b_2, not_1_out, xnor_2_out);
  or or_3 (c_2, B, not_2_out, D);
  or or_4 (e, and_1_out, and_2_out);
  or or_5 (d_2, A, and_3_out, and_4_out, and_5_out, and_6_out);
  or or_6 (f, A, and_7_out, and_8_out, and_9_out);
  or or_7 (g, A, and_8_out, and_3_out, and_4_out);
  _7_Segment_Display u_7_segment_display_1 (.g(g), .f(f), .a(a_2), .b(b_2), .e(e), .d(d_2), .c(c_2));  // open: dp
endmodule
